# Fritzing sketch music-color fritzing (saved by Fritzing 0.9.3b)
breadboards: 1

parts:
  DFRobot_DFPlayer_Mini1 = DFRobot DFPlayer Mini [part_number=DFR0299]
  SP1 = SPEAKER [package=pcb_mount_speaker]
  R1 = Resistor [tolerance=±5% resistance=1k package=THT]
  Part2 = Flora TCS34725 Color Sensor
  Part3 = Arduino Uno (Rev3) - ICSP

nets:
  VCC: DFRobot_DFPlayer_Mini1.VCC, Part3.5V
  N1: DFRobot_DFPlayer_Mini1.RX, R1.Pin_0, R1.Pin_1, Part3.D11_PWM/MOSI
  N2: DFRobot_DFPlayer_Mini1.TX, Part3.D10_PWM/SS
  N3: DFRobot_DFPlayer_Mini1.DAC_L, SP1.-
  N4: DFRobot_DFPlayer_Mini1.SPK_1, SP1.+
  GND: DFRobot_DFPlayer_Mini1.GND-1, DFRobot_DFPlayer_Mini1.GND-2, Part2.GND, Part3.GND
  3.3V: Part2.3.3V, Part3.3V3
  N5: Part2.SDA_3V, Part3.A4/SDA
  N6: Part2.SCL, Part3.A5/SCL

custom parts:
  Flora TCS34725 Color Sensor: Your electronics can now see in dazzling color with this lovely color light sensor. We found the best color sensor on the market, the TCS34725, which has RGB and Clear light sensing elements. An IR blocking filter, integrated on-chip and localized to the color sensing photodiodes, minimizes the IR spectral component of the incoming light and allows color measurements to be made accurately. The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
